# Fritzing sketch hackerRadio (saved by Fritzing 0.9.4)

parts:
  Part1 = Si4713 Stereo FM Transmitter
  U1 = NodeMCU V1.0

nets:
  VIN: Part1.VIN, U1.3V3
  GND: Part1.GND, U1.GND
  N1: Part1.SDA, U1.D1
  N2: Part1.SCL, U1.D2
  N3: Part1.RST, U1.D6

notes:
  <=== TRS Line Leve MIC goes here
  <=== Wire Antenna

custom parts:
  Si4713 Stereo FM Transmitter: Yaaar! Become your very own pirate radio station with this FM radio transmitter. This breakout board, based on the best-of-class Si4713, is an all-in-one stereo audio FM transmitter that can also transmit RDS/RBDS data!
  NodeMCU V1.0: ESP8266 based NodeMCU
